// Logisim project projeto_2 (1).circ as structural Verilog: 9 circuits, main circuit main
module main (
);

  cronometro cronometro_1 ();  // open: out_9, out_10, out_11, out_12, endX, clear, mode, Pause, Clock, DM, UM, DS, US
endmodule

module cronometro (
  input  clear,
  input  Pause,
  input  Clock,
  input  mode,
  input  DM,
  input  UM,
  input  DS,
  input  US,
  output [3:0] out_9,
  output [3:0] out_10,
  output [3:0] out_11,
  output [3:0] out_12,
  output endX
);

  wire comparator_1_eq, comparator_2_eq, comparator_3_eq, mux_1_out_4, mux_2_out_4, mux_3_out_4, mux_4_out_4,
       mux_5_out_4, or_1_out;

  endX endx_1 (.in_1(out_12), .in_2(out_11), .in_3(out_10), .in_4(out_9), .out_5(endX));
  Hex_Digit_Display hex_digit_display_1 (.value(out_9));  // open: dp
  cont_0_5 _0_5_min (.Clock(mux_1_out_4), .Clear(clear), .Dezenas(out_9));
  Hex_Digit_Display hex_digit_display_2 (.value(out_10));  // open: dp
  cont_0_9 _0_9_min (.Clock(mux_2_out_4), .Clear(clear), .Unidades(out_10));
  Comparator #(.width(4)) comparator_1 (.a(out_10), .b(4'b1001), .eq(comparator_1_eq));  // open: gt, lt
  MUX mux_1 (.Q1(DM), .Q2(comparator_1_eq), .S(mode), .out_4(mux_1_out_4));
  Hex_Digit_Display hex_digit_display_3 (.value(out_11));  // open: dp
  cont_0_5 _0_5_sec (.Clock(mux_3_out_4), .Clear(clear), .Dezenas(out_11));
  Comparator #(.width(4)) comparator_2 (.a(out_11), .b(4'b0101), .eq(comparator_2_eq));  // open: gt, lt
  MUX mux_2 (.Q1(UM), .Q2(comparator_2_eq), .S(mode), .out_4(mux_2_out_4));
  Hex_Digit_Display hex_digit_display_4 (.value(out_12));  // open: dp
  cont_0_9 _0_9_sec (.Clock(mux_5_out_4), .Clear(clear), .Unidades(out_12));
  Comparator #(.width(4)) comparator_3 (.a(out_12), .b(4'b1001), .eq(comparator_3_eq));  // open: gt, lt
  MUX mux_3 (.Q1(DS), .Q2(comparator_3_eq), .S(mode), .out_4(mux_3_out_4));
  MUX mux_4 (.Q1(1'b0), .Q2(Clock), .S(or_1_out), .out_4(mux_4_out_4));
  MUX mux_5 (.Q1(US), .Q2(mux_4_out_4), .S(mode), .out_4(mux_5_out_4));
  or or_1 (or_1_out, endX, Pause);
endmodule

module cont_0_9 (
  input  Clock,
  input  Clear,
  output [3:0] Unidades
);

  wire circ_0_9_1_d0, circ_0_9_1_d1, circ_0_9_1_d2, circ_0_9_1_d3;

  D_Flip_Flop d_ff_1 (.clk(Clock), .D(circ_0_9_1_d3), .Q(Unidades[3]), .reset(Clear));  // open: Qn, preset, en
  D_Flip_Flop d_ff_2 (.clk(Clock), .D(circ_0_9_1_d2), .Q(Unidades[2]), .reset(Clear));  // open: Qn, preset, en
  D_Flip_Flop d_ff_3 (.clk(Clock), .D(circ_0_9_1_d1), .Q(Unidades[1]), .reset(Clear));  // open: Qn, preset, en
  circ_0_9 circ_0_9_1 (
    .Q3(Unidades[3]), .Q2(Unidades[2]), .Q1(Unidades[1]), .Q0(Unidades[0]), .D3(circ_0_9_1_d3),
    .D2(circ_0_9_1_d2), .D1(circ_0_9_1_d1), .D0(circ_0_9_1_d0));
  D_Flip_Flop d_ff_4 (.clk(Clock), .D(circ_0_9_1_d0), .Q(Unidades[0]), .reset(Clear));  // open: Qn, preset, en
endmodule

module cont_0_5 (
  input  Clock,
  input  Clear,
  output [3:0] Dezenas
);

  wire circ_0_5_1_d0, circ_0_5_1_d1, circ_0_5_1_d2;

  D_Flip_Flop d_ff_1 (.clk(Clock), .D(circ_0_5_1_d2), .Q(Dezenas[2]), .reset(Clear));  // open: Qn, preset, en
  D_Flip_Flop d_ff_2 (.clk(Clock), .D(circ_0_5_1_d1), .Q(Dezenas[1]), .reset(Clear));  // open: Qn, preset, en
  circ_0_5 circ_0_5_1 (
    .Q2(Dezenas[2]), .Q1(Dezenas[1]), .Q0(Dezenas[0]), .D2(circ_0_5_1_d2), .D1(circ_0_5_1_d1),
    .D0(circ_0_5_1_d0));
  D_Flip_Flop d_ff_3 (.clk(Clock), .D(circ_0_5_1_d0), .Q(Dezenas[0]), .reset(Clear));  // open: Qn, preset, en

  assign Dezenas[3] = 1'b0;
endmodule

module circ_0_9 (
  input  Q3,
  input  Q2,
  input  Q1,
  input  Q0,
  output D3,
  output D2,
  output D1,
  output D0
);

  wire and_1_out, and_2_out, and_3_out, and_4_out, and_5_out, and_6_out, and_7_out, and_8_out, not_1_out,
       not_2_out, not_3_out, not_4_out, not_5_out, not_6_out, not_7_out, not_8_out;

  not not_1 (not_1_out, Q3);
  not not_2 (not_2_out, Q2);
  not not_3 (not_3_out, Q1);
  not not_4 (not_4_out, Q0);
  and and_1 (and_1_out, Q2, Q0);
  and and_2 (and_2_out, Q2, Q1);
  and and_3 (and_3_out, Q3, not_5_out);
  not not_5 (not_5_out, Q0);
  and and_4 (and_4_out, Q1, Q0);
  and and_5 (and_5_out, Q2, not_6_out, not_7_out);
  not not_6 (not_6_out, Q1);
  not not_7 (not_7_out, Q0);
  and and_6 (and_6_out, Q3, not_8_out);
  not not_8 (not_8_out, Q0);
  not not_9 (D0, Q0);
  and and_7 (and_7_out, not_1_out, not_2_out, not_3_out, not_4_out);
  or or_1 (D3, and_7_out, and_8_out);
  and and_8 (and_8_out, Q3, Q0);
  or or_2 (D2, and_1_out, and_2_out, and_3_out);
  or or_3 (D1, and_4_out, and_5_out, and_6_out);
endmodule

module circ_0_5 (
  input  Q2,
  input  Q1,
  input  Q0,
  output D2,
  output D1,
  output D0
);

  wire and_1_out, and_2_out, and_3_out, and_4_out, not_1_out, not_2_out, not_3_out, not_4_out;

  not not_1 (not_1_out, Q2);
  not not_2 (not_2_out, Q1);
  and and_1 (and_1_out, not_1_out, not_2_out, not_3_out);
  not not_3 (not_3_out, Q0);
  and and_2 (and_2_out, Q2, Q0);
  and and_3 (and_3_out, Q1, Q0);
  and and_4 (and_4_out, Q2, not_4_out);
  not not_4 (not_4_out, Q0);
  not not_5 (D0, Q0);
  or or_1 (D2, and_1_out, and_2_out);
  or or_2 (D1, and_3_out, and_4_out);
endmodule

module endX (
  input  [3:0] in_1,
  input  [3:0] in_2,
  input  [3:0] in_3,
  input  [3:0] in_4,
  output out_5
);

  wire comparator_1_eq, comparator_2_eq, comparator_3_eq, comparator_4_eq;

  Comparator #(.width(4)) comparator_1 (.a(in_1), .b(4'b0000), .eq(comparator_1_eq));  // open: gt, lt
  Comparator #(.width(4)) comparator_2 (.a(in_2), .b(4'b0000), .eq(comparator_2_eq));  // open: gt, lt
  Comparator #(.width(4)) comparator_3 (.a(in_3), .b(4'b0000), .eq(comparator_3_eq));  // open: gt, lt
  Comparator #(.width(4)) comparator_4 (.a(in_4), .b(4'b0000), .eq(comparator_4_eq));  // open: gt, lt
  and and_1 (out_5, comparator_1_eq, comparator_2_eq, comparator_3_eq, comparator_4_eq);
endmodule

module MUX (
  input  Q1,
  input  Q2,
  input  S,
  output out_4
);

  wire and_1_out, and_2_out;

  and and_1 (and_1_out, Q1, S);
  and and_2 (and_2_out, Q2, ~S);  // AND_Gate
  or or_1 (out_4, and_1_out, and_2_out);
endmodule

module core (
  input  in_1,
  input  in_2,
  input  in_3,
  input  in_4,
  input  in_5,
  input  in_6,
  input  in_7,
  input  in_8,
  input  Reset,
  input  A3,
  input  A2,
  input  A1,
  input  A0,
  input  B3,
  input  B2,
  input  B1,
  input  B0,
  output A_dead,
  output B_dead
);

  cronometro cronometro_1 (
    .endX(A_dead), .clear(Reset), .DM(in_1), .UM(in_2), .DS(in_3), .US(in_4));  // open: out_9, out_10, out_11, out_12, mode, Pause, Clock
  cronometro cronometro_2 (
    .endX(B_dead), .clear(Reset), .DM(in_5), .UM(in_6), .DS(in_7), .US(in_8));  // open: out_9, out_10, out_11, out_12, mode, Pause, Clock
endmodule
